# Fritzing sketch door-sensor (saved by Fritzing 0.9.10b)
breadboards: 1

parts:
  IC1 = AE-TYBLE16 (300mil) [part_number=K-12339 package="DIP (Dual Inline) [THT]"]
  JP2 = Header 6 [package=1x06-smd-female-v2]
  C1 = Capacitor Polarized [package=cpol-radial-100uf-25v]

nets:
  N1: IC1.DIP2, JP2.5
  N2: IC1.DIP3, JP2.4
  N3: IC1.DIP5, JP2.2
  N4: IC1.DIP6, JP2.1
  N5: IC1.DIP13, JP2.3, C1.-
  N6: IC1.DIP14, JP2.6, C1.+

custom parts:
  AE-TYBLE16 (300mil): AE-TYBLE16 BLE module whose MPU core is nRF51822 as 300mil (7.62mm) breadfriendly width, actual width is 8.0mm
